// Logisim project CPU_LoongArch.circ as structural Verilog
module ALU (
  input  [3:0] alu_op,
  input  [31:0] src1,
  input  [31:0] src2,
  output [31:0] alu_res
);

  wire adder_1_cout, and_1_out, and_3_out, multiplexer_2_out, multiplexer_3_out, not_2_out, slt_out,
       slt_sltu_out, xor_1_out;
  wire [1:1] alu_res_sel;
  wire [31:0] adder_1_out, and_2_out, bit_extender_1_out, multiplexer_1_out, multiplexer_4_out, not_1_out,
       not_3_out, or_1_out, shifter_1_out, shifter_3_out, shifter_4_out, xor_2_out;

  Multiplexer #(.width(32)) multiplexer_1 (.in0(src2), .in1(not_1_out), .out(multiplexer_1_out), .sel(alu_op[0]));
  assign not_1_out = ~src2;  // NOT_Gate not_1, 32 bits wide
  xor xor_1 (xor_1_out, src1[31], src2[31]);
  or shift_ifornot (alu_res_sel[1], alu_op[2], alu_op[3]);
  and and_1 (and_1_out, src1[31], xor_1_out);
  not not_2 (not_2_out, xor_1_out);
  Multiplexer multiplexer_2 (.in0(1'b0), .in1(1'b1), .out(multiplexer_2_out), .sel(alu_op[0]));
  Adder #(.width(32)) adder_1 (
    .a(src1), .b(multiplexer_1_out), .out(adder_1_out), .cin(multiplexer_2_out), .cout(adder_1_cout));
  Multiplexer multiplexer_3 (.in0(1'b1), .in1(1'b0), .out(multiplexer_3_out), .sel(adder_1_cout));
  Shifter #(.width(32)) shifter_1 (.in(src1), .\dist (src2[4:0]), .out(shifter_1_out));
  Shifter #(.shift("lr"), .width(32)) shifter_2 (.in(src1), .\dist (src2[4:0]), .out(shifter_1_out));
  Shifter #(.shift("ar"), .width(32)) shifter_3 (.in(src1), .\dist (src2[4:0]), .out(shifter_3_out));
  Shifter #(.width(32)) shifter_4 (.in(src2), .\dist (5'b01100), .out(shifter_4_out));
  assign and_2_out = src1 & src2;  // AND_Gate and_2, 32 bits wide
  assign or_1_out = src1 | src2;  // OR_Gate or_1, 32 bits wide
  assign xor_2_out = src1 ^ src2;  // XOR_Gate xor_2, 32 bits wide
  and and_3 (and_3_out, adder_1_out[31], not_2_out);
  or slt (slt_out, and_3_out, and_1_out);
  Multiplexer #(.select(2), .width(32)) multiplexer_4 (
    .in0(src2), .in1(shifter_1_out), .in2(shifter_1_out), .in3(shifter_3_out), .out(multiplexer_4_out),
    .sel(alu_op[3:2]));
  assign not_3_out = ~or_1_out;  // NOT_Gate not_3, 32 bits wide
  or slt_sltu (slt_sltu_out, slt_out, multiplexer_3_out);
  assign bit_extender_1_out = {{31{1'b0}}, slt_sltu_out};  // Bit_Extender bit_extender_1
  Multiplexer #(.select(3), .width(32)) multiplexer_5 (
    .in0(adder_1_out), .in1(bit_extender_1_out), .in2(multiplexer_4_out), .in3(shifter_4_out),
    .in4(and_2_out), .in5(or_1_out), .in6(not_3_out), .in7(xor_2_out), .out(alu_res));  // open: sel

  // Other names for the same wires on the sheet: shift_sel[1:0] = alu_op[3:2]; alu_res_sel[0] = alu_op[1]

  // Notes on the sheet:
  //   0位:加法还是减法  为1指令:sub.w,slt,sltu
  //   slt逻辑
  //   1位:是不是slt(u)，结果选择  为1指令:slt,sltu
  //   2-3位:移位操作，00不是移位  01逻辑左  10逻辑右  11算术右
  //   if (A[31] != B[31])  A < B = A[31]
  //   else  A < B = (A - B)[31]
  //   sel_notsrc2
  //   为1的指令:sub.w,slt,sltu
  //   alu_op之后应该会以部分指令编码的形式直接给出，现在做的控制信号只是意思意思的
  //   为1的指令:sub.w,slt,sltu
  //   sel_cin
  //   sel_cout
  //   sltu，相减的cout为0的时候置位
  //   1:slt,sltu
  //   alu_op来选择
  //   2:slli.w,srli.w,srai.w
endmodule

module br_unit (
  input  [2:0] br_op,
  input  valid,
  input  block_id,
  input  [25:0] offs,
  input  [31:0] PC,
  input  [31:0] RD1,
  input  [31:0] RD2,
  output br_taken_cancle,
  output br_taken,
  output [31:0] br_target
);

  wire beq_out, bne_out, comparator_1_eq, or_1_out;
  wire [31:0] bit_extender_1_out, bit_extender_2_out, multiplexer_1_out, multiplexer_2_out, shifter_1_out;

  assign bit_extender_1_out = {{16{offs[25]}}, offs[25:10]};  // Bit_Extender bit_extender_1
  assign bit_extender_2_out = {{6{offs[25]}}, offs};  // Bit_Extender bit_extender_2
  Comparator #(.width(32)) comparator_1 (.a(RD1), .b(RD2), .eq(comparator_1_eq));  // open: gt, lt
  Multiplexer #(.width(32)) multiplexer_1 (
    .in0(bit_extender_1_out), .in1(bit_extender_2_out), .out(multiplexer_1_out), .sel(br_op[1]));
  Shifter #(.width(32)) shifter_1 (.in(multiplexer_1_out), .\dist (5'b00010), .out(shifter_1_out));
  and beq (beq_out, comparator_1_eq, br_op[0], valid);
  and bne (bne_out, ~comparator_1_eq, br_op[0], ~valid);  // AND_Gate
  Multiplexer #(.width(32)) multiplexer_2 (.in0(PC), .in1(RD1), .out(multiplexer_2_out), .sel(br_op[2]));
  or or_1 (or_1_out, beq_out, bne_out);
  Adder #(.width(32)) adder_1 (.a(shifter_1_out), .b(multiplexer_2_out), .out(br_target));  // open: cin, cout
  or or_2 (br_taken, br_op[2], br_op[1], or_1_out);
  and and_1 (br_taken_cancle, ~block_id, br_taken);  // AND_Gate

  // Other names for the same wires on the sheet: br_op_0 = br_op[0]; br_op_1 = br_op[1]; br_op_2 = br_op[2]

  // Notes on the sheet:
  //   假设br_op = 0:bne  1:beq  2:b  3:bl  4:jirl
  //   单纯判断是否相等就行
  //   br_op_0用于区分bne还是beq用于判断跳转
  //   b、bl、jirl指令是无条件跳转，br_taken为1
  //   br_op_1用于区分是bne、beq还是b、bl  用于判断是否无条件跳转
  //   br_op_2为1的时候说明是jirl，无条件跳转，并且使用RD1 + offs的结果
endmodule

module rk_rj_equal_rd (
  input  [4:0] rd_exe,
  input  [4:0] rd_mem,
  input  [4:0] rd_wb,
  input  [4:0] rk_id,
  input  [4:0] rj_id,
  input  inst_is_ldw_exe,
  input  [31:0] rdata1,
  input  [31:0] forward_exe,
  input  [31:0] forward_mem,
  input  [31:0] forward_wb,
  input  [31:0] rdata2,
  output block_id,
  output [1:0] sel_rj_forward,
  output [1:0] sel_rkd_forward
);

  wire comparator_1_eq, comparator_2_eq, comparator_3_eq, comparator_4_eq, comparator_5_eq, comparator_6_eq,
       or_1_out;
  wire [31:0] multiplexer_1_out, multiplexer_2_out;

  Comparator #(.width(5)) comparator_1 (.a(rd_exe), .b(rk_id), .eq(comparator_1_eq));  // open: gt, lt
  Comparator #(.width(5)) comparator_2 (.a(rd_mem), .b(rk_id), .eq(comparator_2_eq));  // open: gt, lt
  Comparator #(.width(5)) comparator_3 (.a(rd_wb), .b(rk_id), .eq(comparator_3_eq));  // open: gt, lt
  Comparator #(.width(5)) comparator_4 (.a(rd_exe), .b(rj_id), .eq(comparator_4_eq));  // open: gt, lt
  Comparator #(.width(5)) comparator_5 (.a(rd_mem), .b(rj_id), .eq(comparator_5_eq));  // open: gt, lt
  Comparator #(.width(5)) comparator_6 (.a(rd_wb), .b(rj_id), .eq(comparator_6_eq));  // open: gt, lt
  or or_1 (or_1_out, comparator_1_eq, comparator_4_eq);
  Priority_Encoder #(.select(2)) priority_encoder_1 (
    .in1(comparator_4_eq), .in2(comparator_5_eq), .in3(comparator_6_eq), .out(sel_rj_forward));  // open: in0, gs, en_out, en_in
  Priority_Encoder #(.select(2)) priority_encoder_2 (
    .in1(comparator_1_eq), .in2(comparator_2_eq), .in3(comparator_3_eq), .out(sel_rkd_forward));  // open: in0, gs, en_out, en_in
  and and_1 (block_id, or_1_out, inst_is_ldw_exe);
  Multiplexer #(.select(2), .width(32)) multiplexer_1 (
    .in0(rdata1), .in1(forward_exe), .in2(forward_mem), .in3(forward_wb), .out(multiplexer_1_out),
    .sel(sel_rj_forward));
  Multiplexer #(.select(2), .width(32)) multiplexer_2 (
    .in0(rdata2), .in1(forward_exe), .in2(forward_mem), .in3(forward_wb), .out(multiplexer_2_out),
    .sel(sel_rkd_forward));

  // Notes on the sheet:
  //   别忘了rk_id和rj_id不能是0，是0的话就不用阻塞了
  //   信号传进来之前都需要和伴随的阶段中的valid信号做与操作，确保是有效信号的寄存器目标
  //   这里应该是通用寄存器堆门口的位置的设计了
  //   这里优先编码器的顺序和我设计图中的优先级是不一样的，只是碍于这个软件的优先编码器的使用方式而已了
  //   0：表示没有冲突 1：表示exe阶段有冲突，且冲突等级最高 2：表示mem阶段有冲突，冲突等级中等 3：表示wb阶段有冲突，且冲突等级最低
endmodule
